// Digital circuit ALU.dig as structural Verilog
module ALU (
  input  [15:0] I,
  input  [15:0] X,
  input  [15:0] Y,
  output [15:0] O
);

  ArithUnit arithunit_1 (.X(X), .Y(Y), .OP(I[1:0]), .ZX(I[2]), .ZY(I[3]), .O(O));
endmodule
