// Digital circuit computer.dig as structural Verilog
module computer (
  input  clk
);

  wire [15:0] alu_1_o, counterpreset_1_out, ram_1_a_2, ram_1_d_3, ram_1_m_2, rom_1_d, undriven;

  CounterPreset #(.Bits(16)) counterpreset_1 (
    .C(clk), .in(ram_1_a_2), .out(counterpreset_1_out));  // open: en, dir, ld, clr, ovf
  ROM #(.AddrBits(15), .Bits(16)) rom_1 (.A(counterpreset_1_out[14:0]), .sel(1'b1), .D(rom_1_d));
  ALU alu_1 (.I(rom_1_d), .X(ram_1_d_3), .Y(ram_1_m_2), .O(alu_1_o));
  RAM ram_1 (
    .A(undriven), .D(alu_1_o), .C(clk), .A_2(ram_1_a_2), .D_3(ram_1_d_3), .M_2(ram_1_m_2));  // open: a_3, d_2, m
  // Pins of 15 and 16 bits meet at counterpreset_1_out
endmodule
